# Fritzing sketch circuitsketch (saved by Fritzing 0.9.3b)

parts:
  Part1 = Arduino Leonardo (Rev3b)
  U2 = POT [package=pot_alpha_rv16af-20]
  U3 = POT [package=pot_alpha_rv16af-20]
  GY1 = GY-521 (MPU-6050) [form="♀ (female)" package=THT]
  S1 = Pushbutton [package=THT]
  S2 = Pushbutton [package=THT]
  S3 = Pushbutton [package=THT]
  S4 = Pushbutton [package=THT]
  S5 = Pushbutton [package=THT]
  S6 = Pushbutton [package=THT]
  S7 = Pushbutton [package=THT]
  S8 = Pushbutton [package=THT]

nets:
  N1: Part1.D4/A6, S6.leg0
  N2: Part1.D5_PWM, S5.leg0
  N3: Part1.D6_PWM/A7, S4.leg0
  N4: Part1.D7, S3.leg0
  N5: Part1.5V, GY1.pin1
  N6: Part1.GND, U2.E, GY1.pin2, S1.leg1, S2.leg1, S3.leg1, S4.leg1, S5.leg1, S6.leg1, S7.leg1, S8.leg1
  N7: Part1.A0, U2.S
  N8: Part1.A1, U3.S
  N9: Part1.D8/A8, S2.leg0
  N10: Part1.D9_PWM/A9, S1.leg0
  N11: Part1.D10_PWM/A10, S7.leg0
  N12: Part1.D11_PWM, S8.leg0
  N13: Part1.SDA, GY1.pin4
  N14: Part1.SCL, GY1.pin3

custom parts:
  GY-521 (MPU-6050): Placa GY-521 basada en conjunto de acelerómetro+giroscopios MPU-6050
